# Fritzing sketch BackgroundLed_Sketch (saved by Fritzing 0.9.9b)
breadboards: 1

parts:
  MCU1 = Raspberry Pi Zero
  U2 = MCP4725 [package=SOT23-6]
  VM2 = Multimeter (DC Voltage)
  U1 = MCP4725 [package=SOT23-6]
  VM1 = Multimeter (DC Voltage)
  LED1 = smd LED [color="White (6500K)" package="0603 [SMD]"]
  LED2 = smd LED [color="White (6500K)" package="0603 [SMD]"]
  S1 = Momentary Switch [package=tactile-pth]
  R1 = Resistor [tolerance=±5% power=0.25 resistance=330 package=THT]
  R2 = Resistor [tolerance=±5% power=0.25 resistance=330 package=THT]

nets:
  VDD: MCU1.pin_2, MCU1.pin_4, U2.VDD, U2.AO, U1.VDD
  N1: MCU1.pin_3, U2.SDA, U1.SDA
  N2: MCU1.pin_5, U2.SCL, U1.SCL
  VSS: MCU1.pin_6, MCU1.pin_25, MCU1.pin_39, U2.VSS, VM2.COM_Probe, U1.VSS, VM1.COM_Probe, LED1.cathode, LED2.cathode, S1.3
  N3: MCU1.pin_11, S1.1
  N4: MCU1.pin_12, R1.Pin_0
  N5: MCU1.pin_13, R2.Pin_0
  N6: U2.VOUT, VM2.V_Probe
  N7: U1.VOUT, VM1.V_Probe
  N8: LED1.anode, R2.Pin_1
  N9: LED2.anode, R1.Pin_1
