# Fritzing sketch FritzMeter_Sketch (saved by Fritzing 0.9.9b)
breadboards: 1

parts:
  MCU1 = Raspberry Pi Zero
  U2 = MCP4725 [package=SOT23-6]
  VM2 = Multimeter (DC Voltage)
  U1 = MCP4725 [package=SOT23-6]
  VM1 = Multimeter (DC Voltage)

nets:
  VDD: MCU1.pin_2, MCU1.pin_4, U2.VDD, U2.AO, U1.VDD
  N1: MCU1.pin_3, U2.SDA, U1.SDA
  N2: MCU1.pin_5, U2.SCL, U1.SCL
  VSS: MCU1.pin_6, MCU1.pin_25, MCU1.pin_39, U2.VSS, VM2.COM_Probe, U1.VSS, VM1.COM_Probe
  N3: U2.VOUT, VM2.V_Probe
  N4: U1.VOUT, VM1.V_Probe
